// Logisim project y86.circ as structural Verilog
module main (
  input  Reset,
  output [3:0] out_2,
  output [3:0] out_3,
  output [31:0] out_4,
  output [3:0] out_5,
  output [3:0] out_6,
  output [31:0] out_7,
  output [31:0] out_8,
  output [31:0] out_9,
  output [31:0] out_10,
  output [31:0] out_11,
  output [31:0] out_12,
  output [31:0] out_13,
  output [31:0] out_14,
  output [31:0] out_15,
  output [31:0] out_16
);

  wire and_1_out, Clock_out, nor_1_out, not_1_out, OF, select_read_read, select_write_write, SF, ZF;
  wire [1:0] Stat_q, Status_Update_new_stat;
  wire [3:0] select_dstE_deste, select_dstM_dst_m, select_srcA_srca, select_srcB_out_3;
  wire [7:0] imem_1_p4, imem_1_p5, imem_1_p6, imem_1_p7, imem_1_p8, imem_1_p9, imem_1_p10, imem_1_p11,
       imem_1_p12;
  wire [31:0] memory_address_0, memory_address_1, PC_q, select_aluA_alua_0, select_aluA_alua_1,
       select_aluB_alub_0, select_aluB_alub_1, select_data_data_0, select_data_data_1, valP;

  and and_1 (and_1_out, Clock_out, nor_1_out);
  Clock Clock (.out(Clock_out));
  Register #(.width(32)) PC (.D(out_4), .Q(PC_q), .clk(and_1_out), .clr(Reset));  // open: en
  nor nor_1 (nor_1_out, Stat_q[1], Stat_q[0]);
  not not_1 (not_1_out, and_1_out);
  Register #(.width(2)) Stat (.D(Status_Update_new_stat), .Q(Stat_q), .clk(not_1_out));  // open: en, clr
  // imem imem_1: pin names not known; wires that end beside it: out_4, PC_q, {out_2, out_3}, imem_1_p4, imem_1_p5, imem_1_p6, imem_1_p7, imem_1_p8, imem_1_p9, imem_1_p10, imem_1_p11, imem_1_p12, out_10
  Align align_1 (
    .B1(imem_1_p4), .B2(imem_1_p5), .B3(imem_1_p6), .B4(imem_1_p7), .B5(imem_1_p8), .B6(imem_1_p9),
    .B7(imem_1_p10), .B8(imem_1_p11), .B9(imem_1_p12), .rB(out_5), .rA(out_6), .valC_1(out_8), .valC_0(out_7));  // open: NeedRegs
  Status_Update Status_Update (
    .icode(out_2), .memory_address_0(memory_address_0), .memory_address_1(memory_address_1),
    .new_stat(Status_Update_new_stat));
  srcA select_srcA (.rA(out_6), .icode(out_2), .srcA(select_srcA_srca));
  srcB select_srcB (.rB(out_5), .in_1(out_2), .out_3(select_srcB_out_3));
  dstE select_dstE (.destE(select_dstE_deste), .icode(out_2), .rB(out_5));
  dstM select_dstM (.rA(out_6), .icode(out_2), .dst_M(select_dstM_dst_m));
  // regfile regfile_1: pin names not known; wires that end beside it: select_srcA_srca, select_srcB_out_3, select_dstE_deste, out_10, out_9, select_dstM_dst_m, out_12, out_11, not_1_out, Reset, out_14, out_13, out_16, out_15
  select_aluA select_aluA (
    .icode(out_2), .icode_2(out_2), .aluA_0(select_aluA_alua_0), .aluA_1(select_aluA_alua_1),
    .valA_0(out_13), .valA_1(out_14), .valC_0(out_7), .valC_1(out_7));
  select_aluB select_aluB (
    .icode(out_2), .aluB_0(select_aluB_alub_0), .icode_2(out_2), .aluB_1(select_aluB_alub_1),
    .valB_0(out_15), .valB_1(out_16));
  alu ALU (
    .aluA_1(select_aluA_alua_0), .aluA_0(select_aluA_alua_1), .aluB_1(select_aluB_alub_1),
    .aluB_0(select_aluB_alub_0), .out_6(ZF), .out_7(SF), .out_8(OF), .ALUfun(out_3), .valE_1(out_10),
    .valE_0(out_9));
  select_read select_read (.icode(out_2), .read(select_read_read));
  select_write select_write (.icode(out_2), .write(select_write_write));
  select_address select_address (
    .address_0(memory_address_0), .address_1(memory_address_1), .icode_2(out_2), .icode(out_2),
    .valE_0(out_9), .valE_1(out_10), .valA_0(out_13), .valA_1(out_14));
  select_data select_data (
    .icode(out_2), .icode_2(out_2), .data_1(select_data_data_1), .data_0(select_data_data_0), .valP_0(valP),
    .valA_0(out_13), .valA_1(out_14));
  // dmem dmem_1: pin names not known; wires that end beside it: memory_address_1, memory_address_0, select_data_data_1, select_data_data_0, select_read_read, select_write_write, not_1_out, Reset, out_12, out_11
  pc_inc_with_jump_PC_Increment pc_increment_1 (
    .icode(out_2), .PC(PC_q), .in_3(ZF), .in_4(SF), .in_5(OF), .Val_P(valP));
  Register #(.width(32)) PChold (.D(valP), .Q(out_4), .clk(not_1_out), .clr(Reset));  // open: en

  // Other names for the same wires on the sheet: ifun[3:0] = out_3; icode[3:0] = out_2; new_PC[31:0] = out_4;
  //   rA[3:0] = out_6; rB[3:0] = out_5; valA_0[31:0] = out_13; valA_1[31:0] = out_14; valB_0[31:0] = out_15;
  //   valB_1[31:0] = out_16; valC_0[31:0] = out_7; valC_1[31:0] = out_8; valE_0[31:0] = out_9; valE_1[31:0] = out_10;
  //   valM_0[31:0] = out_11; valM_1[31:0] = out_12

  // Notes on the sheet:
  //   Fetch Stage:
  //   rA, rB, valC,
  //   and valP
  //   icode, ifun,
  //   are computed.
  //   Memory
  //   Decode stage:
  //   srcA and srcB
  //   are found based 
  //   on the icode.
  //   From srcA and srcB
  //   valA and valB are
  //   computed.
  //   Execute Stage
  //   The core instruction is executed,
  //   computing valE and condition codes.
  //   still have not added fixed pc inc
  //   is sent to the program counter.
  //   PC Inc
  //   PC Update stage:
  //   The held value in the program counter hold
  //   Memory and writeback stage:
endmodule

module Align (
  input  [7:0] B1,
  input  [7:0] B2,
  input  [7:0] B3,
  input  [7:0] B4,
  input  [7:0] B5,
  input  [7:0] B6,
  input  [7:0] B7,
  input  [7:0] B8,
  input  [7:0] B9,
  input  NeedRegs,
  output [3:0] rB,
  output [3:0] rA,
  output [31:0] valC_1,
  output [31:0] valC_0
);

  wire [3:0] icode;

  Multiplexer #(.select(4)) multiplexer_1 (
    .in0(1'b0), .in1(1'b0), .in2(1'b1), .in3(1'b1), .in4(1'b1), .in5(1'b1), .in6(1'b1), .in7(1'b0),
    .in8(1'b0), .in9(1'b0), .in10(1'b1), .in11(1'b1), .in12(1'b1), .in13(1'b1), .in14(1'b1), .in15(1'b1),
    .out(NeedRegs), .sel(icode));  // open: en

  assign rA = B1[7:4];
  assign rB = B1[3:0];
  assign valC_0 = {B5, B4, B3, B2};
  assign valC_1 = {B6, B7, B8, B9};

  // Notes on the sheet:
  //   valC_0 is lower 32 bits, while valC_1 is upper 32, more significant, bits
endmodule

module PC_Increment (
  input  [3:0] icode,
  input  in_2,
  input  in_3,
  input  in_4,
  input  [31:0] PC,
  output [31:0] Val_P
);

  wire [31:0] multiplexer_1_out;

  Multiplexer #(.select(4), .width(32), .enable("false")) multiplexer_1 (
    .in0({32{1'b0}}), .in1(32'h1), .in2(32'h2), .in3(32'ha), .in4(32'ha), .in5(32'ha), .in6(32'h2),
    .in7(32'h9), .in8(32'h9), .in9(32'h1), .in10(32'h2), .in11(32'h2), .out(multiplexer_1_out), .sel(icode));  // open: in12, in13, in14, in15
  Adder #(.width(32)) adder_1 (.a(multiplexer_1_out), .b(PC), .out(Val_P));  // open: cin, cout

  // Other names for the same wires on the sheet: of = in_4; sf = in_3; zf = in_2

  // Notes on the sheet:
  //   PC Increment
  //   Input: icode, PC
  //   Output: The next value for PC, or Val P
  //   PC + Instruction Length
endmodule

module srcA (
  input  [3:0] rA,
  input  [3:0] icode,
  output [3:0] srcA
);

  Multiplexer #(.select(4), .width(4), .enable("false")) multiplexer_1 (
    .in0(4'b1111), .in1(4'b1111), .in2(rA), .in3(4'b1111), .in4(rA), .in5(4'b1111), .in6(rA), .in7(4'b1111),
    .in8(4'b1111), .in9(4'b1111), .in10(rA), .in11(4'b0100), .out(srcA), .sel(icode));  // open: in12, in13, in14, in15
endmodule

module srcB (
  input  [3:0] in_1,
  input  [3:0] rB,
  output [3:0] out_3
);

  Multiplexer #(.select(4), .width(4), .enable("false")) multiplexer_1 (
    .in0(4'b1111), .in1(4'b1111), .in2(4'b1111), .in3(4'b1111), .in4(rB), .in5(rB), .in6(rB), .in7(4'b1111),
    .in8(4'b0100), .in9(4'b0100), .in10(4'b0100), .in11(4'b0100), .out(out_3), .sel(in_1));  // open: in12, in13, in14, in15

  // Notes on the sheet:
  //   all of the constants labeled 4 want to access the value in the %rsp
endmodule

module dstE (
  input  [3:0] rB,
  input  [3:0] icode,
  output [3:0] destE
);

  Multiplexer #(.select(4), .width(4), .enable("false")) multiplexer_1 (
    .in0(4'b1111), .in1(4'b1111), .in2(rB), .in3(rB), .in4(4'b1111), .in5(4'b1111), .in6(rB), .in7(4'b1111),
    .in8(4'b0100), .in9(4'b0100), .in10(4'b0100), .in11(4'b0100), .out(destE), .sel(icode));  // open: in12, in13, in14, in15

  // Notes on the sheet:
  //   Add register names to this mux
endmodule

module dstM (
  input  [3:0] rA,
  input  [3:0] icode,
  output [3:0] dst_M
);

  Multiplexer #(.select(4), .width(4), .enable("false")) multiplexer_1 (
    .in0(4'b1111), .in1(4'b1111), .in2(4'b1111), .in3(4'b1111), .in4(4'b1111), .in5(rA), .in6(4'b1111),
    .in7(4'b1111), .in8(4'b1111), .in9(4'b1111), .in10(4'b1111), .in11(4'b1111), .in12(rA), .out(dst_M),
    .sel(icode));  // open: in13, in14, in15

  // Notes on the sheet:
  //   Add register names
endmodule

module select_aluA (
  input  [31:0] valA_0,
  input  [31:0] valA_1,
  input  [31:0] valC_0,
  input  [31:0] valC_1,
  input  [3:0] icode,
  input  [3:0] icode_2,
  output [31:0] aluA_0,
  output [31:0] aluA_1
);

  Multiplexer #(.select(4), .width(32), .enable("false")) multiplexer_1 (
    .in0({32{1'b0}}), .in1({32{1'b0}}), .in2(valA_0), .in3(valC_0), .in4(valC_0), .in5(valC_0), .in6(valA_0),
    .in7({32{1'b0}}), .in8(32'h8), .in9(32'h8), .in10(32'h8), .in11(32'h8), .out(aluA_0), .sel(icode));  // open: in12, in13, in14, in15
  Multiplexer #(.select(4), .width(32), .enable("false")) multiplexer_2 (
    .in0({32{1'b0}}), .in1({32{1'b0}}), .in2(valA_1), .in3(valC_1), .in4(valC_1), .in5(valC_1), .in6(valA_1),
    .in7({32{1'b0}}), .in8({32{1'b0}}), .in9({32{1'b0}}), .in10({32{1'b0}}), .in11({32{1'b0}}), .out(aluA_1),
    .sel(icode_2));  // open: in12, in13, in14, in15

  // Notes on the sheet:
  //   conflict: cmov and rmmov have the same icode but send diffent aluA values
  //   less signifcant 32 bits
  //   more signifcant 32 bits
endmodule

module select_aluB (
  input  [31:0] valB_0,
  input  [31:0] valB_1,
  input  [3:0] icode,
  input  [3:0] icode_2,
  output [31:0] aluB_0,
  output [31:0] aluB_1
);

  wire [31:0] valB_1_t;

  Multiplexer #(.select(4), .width(32), .enable("false")) multiplexer_1 (
    .in0({32{1'b0}}), .in1({32{1'b0}}), .in2({32{1'b0}}), .in3({32{1'b0}}), .in4(valB_0), .in5(valB_0),
    .in6(valB_0), .in7({32{1'b0}}), .in8(valB_0), .in9(valB_0), .in10(valB_0), .in11(valB_0), .out(aluB_0),
    .sel(icode));  // open: in12, in13, in14, in15
  Multiplexer #(.select(4), .width(32), .enable("false")) multiplexer_2 (
    .in0({32{1'b0}}), .in1({32{1'b0}}), .in2({32{1'b0}}), .in3({32{1'b0}}), .in4(valB_1_t), .in5(valB_1_t),
    .in6(valB_1_t), .in7({32{1'b0}}), .in8(valB_1_t), .in9(valB_1_t), .in10(valB_1_t), .in11(valB_1_t),
    .out(aluB_1), .sel(icode_2));  // open: in12, in13, in14, in15

  // Other names for the same wires on the sheet: vaB_1[31:0] = valB_1
endmodule

module select_read (
  input  [3:0] icode,
  output read
);

  Multiplexer #(.select(4), .enable("false")) multiplexer_1 (
    .in0(1'b0), .in1(1'b0), .in2(1'b0), .in3(1'b0), .in4(1'b0), .in5(1'b1), .in6(1'b1), .in7(1'b0),
    .in8(1'b0), .in9(1'b1), .in10(1'b0), .in11(1'b0), .out(read), .sel(icode));  // open: in12, in13, in14, in15

  // Notes on the sheet:
  //   Select the read command of the given instruction
endmodule

module select_write (
  input  [3:0] icode,
  output write
);

  Multiplexer #(.select(4), .enable("false")) multiplexer_1 (
    .in0(1'b0), .in1(1'b0), .in2(1'b0), .in3(1'b0), .in4(1'b1), .in5(1'b0), .in6(1'b1), .in7(1'b0),
    .in8(1'b1), .in9(1'b0), .in10(1'b1), .in11(1'b0), .out(write), .sel(icode));  // open: in12, in13, in14, in15
endmodule

module select_address (
  input  [31:0] valE_0,
  input  [31:0] valE_1,
  input  [31:0] valA_0,
  input  [3:0] icode,
  input  [31:0] valA_1,
  input  [3:0] icode_2,
  output [31:0] address_0,
  output [31:0] address_1
);

  Multiplexer #(.select(4), .width(32), .enable("false")) multiplexer_1 (
    .in0({32{1'b0}}), .in1({32{1'b0}}), .in2({32{1'b0}}), .in3(valE_0), .in4(valE_0), .in5(valE_0),
    .in6({32{1'b0}}), .in7({32{1'b0}}), .in8(valE_0), .in9(valE_0), .in10(valE_0), .in11(valA_0),
    .out(address_0), .sel(icode));  // open: in12, in13, in14, in15
  Multiplexer #(.select(4), .width(32), .enable("false")) multiplexer_2 (
    .in0({32{1'b0}}), .in1({32{1'b0}}), .in2({32{1'b0}}), .in3(valE_1), .in4(valE_1), .in5(valE_1),
    .in6({32{1'b0}}), .in7({32{1'b0}}), .in8(valE_1), .in9(valE_1), .in10(valE_1), .in11(valA_1),
    .out(address_1), .sel(icode_2));  // open: in12, in13, in14, in15
endmodule

module select_data (
  input  [31:0] valP_0,
  input  [3:0] icode,
  input  [31:0] valA_0,
  input  [31:0] valA_1,
  input  [3:0] icode_2,
  output [31:0] data_1,
  output [31:0] data_0
);

  wire [31:0] undriven;

  Multiplexer #(.select(4), .width(32), .enable("false")) multiplexer_1 (
    .in0({32{1'b0}}), .in1({32{1'b0}}), .in2({32{1'b0}}), .in3({32{1'b0}}), .in4(valA_1), .in5({32{1'b0}}),
    .in6({32{1'b0}}), .in7(undriven), .in8({32{1'b0}}), .in9({32{1'b0}}), .in10(valA_1), .in11({32{1'b0}}),
    .out(data_1), .sel(icode));  // open: in12, in13, in14, in15
  Multiplexer #(.select(4), .width(32), .enable("false")) multiplexer_2 (
    .in0({32{1'b0}}), .in1({32{1'b0}}), .in2({32{1'b0}}), .in3({32{1'b0}}), .in4(valA_0), .in5({32{1'b0}}),
    .in6({32{1'b0}}), .in7({32{1'b0}}), .in8(valP_0), .in9({32{1'b0}}), .in10(valA_0), .in11({32{1'b0}}),
    .out(data_0), .sel(icode_2));  // open: in12, in13, in14, in15
endmodule

module Status_Update (
  input  [3:0] icode,
  input  [31:0] memory_address_0,
  input  [31:0] memory_address_1,
  output [1:0] new_stat
);

  wire [31:0] and_1_out;

  Multiplexer #(.select(4), .width(2), .enable("false")) multiplexer_1 (
    .in0(2'b11), .in1(2'b00), .in2(2'b00), .in3(2'b00), .in4(2'b00), .in5(2'b00), .in6(2'b00), .in7(2'b00),
    .in8(2'b00), .in9(2'b00), .in10(2'b00), .in11(2'b00), .in12(2'b01), .in13(2'b01), .in14(2'b01),
    .in15(2'b01), .out(new_stat), .sel(icode));
  assign and_1_out = 32'hffffff81 & memory_address_0;  // AND_Gate and_1, 32 bits wide

  // Notes on the sheet:
  //   any memory value greater than 0x80 is invalid
  //   Checks to see if instruction is invalid by checking icode
  //   Also triggers halt if icode is 00
  //   Memory address 1 shouldn't have a role to play within selecting a spot in memory to store a value, only the first bit is used
  //   somehow AND the address with a constant to detect numbers over 0x81, then change the stat register appropriately
  //   Input:
  //   Output:
  //   00 - normal
  //   11 - halt
  //   01 - invalid instruction
  //   Status Update:
  //   icode, some memory stuff
  //   The new status of the CPU:
  //   10 - invalid memory address
endmodule
